// Digital circuit Decoder7.dig as structural Verilog
module Decoder7 (
  input  D3,
  input  D2,
  input  D1,
  input  D0,
  output Sa,
  output Sb
);

  wire and_1_out, and_2_out, and_3_out, and_4_out, and_5_out, and_6_out, and_7_out, and_8_out, and_9_out,
       and_10_out, and_11_out, not_1_out, not_2_out, not_3_out, not_4_out;

  not not_1 (not_1_out, D3);
  not not_2 (not_2_out, D2);
  not not_3 (not_3_out, D1);
  not not_4 (not_4_out, D0);
  and and_1 (and_1_out, not_1_out, D1);
  and and_2 (and_2_out, D2, D1);
  and and_3 (and_3_out, not_2_out, not_4_out);
  and and_4 (and_4_out, not_1_out, D2, D0);
  and and_5 (and_5_out, not_2_out, not_3_out, D3);
  and and_6 (and_6_out, not_2_out, not_3_out);
  and and_7 (and_7_out, D3, D2, not_4_out);
  and and_8 (and_8_out, D0, D1, not_1_out);
  and and_9 (and_9_out, not_1_out, not_3_out, not_4_out);
  or or_1 (Sa, and_1_out, and_4_out, and_2_out, and_5_out, and_3_out, and_7_out);
  and and_10 (and_10_out, not_2_out, not_4_out);
  and and_11 (and_11_out, D3, not_3_out, D0);
  or or_2 (Sb, and_9_out, and_8_out, and_11_out, and_6_out, and_10_out);
endmodule
