// Digital circuit Fulladder.dig as structural Verilog
module Fulladder (
  input  A,
  input  B,
  input  Cin,
  output S,
  output Count
);

  wire and_1_out, and_2_out, xor_1_out;

  xor xor_1 (xor_1_out, A, B);
  and and_1 (and_1_out, A, B);
  xor xor_2 (S, Cin, xor_1_out);
  and and_2 (and_2_out, Cin, xor_1_out);
  or or_1 (Count, and_2_out, and_1_out);
endmodule
