// Digital circuit Sub4.dig as structural Verilog
module Sub4 (
  input  X0,
  input  X1,
  input  X2,
  input  X3,
  input  Y3,
  input  Y2,
  input  Y1,
  input  Y0,
  output S0,
  output S1,
  output S2,
  output S3,
  output Count
);

  wire fulladder_1_count, fulladder_2_count, fulladder_3_count, not_1_out, not_2_out, not_3_out, not_4_out;

  Seven_Seg_Hex seven_seg_hex_1 (.d({X3, X2, X1, X0}), .dp(1'b0));
  not not_1 (not_1_out, Y0);
  Fulladder fulladder_1 (.A(X0), .B(not_1_out), .Cin(1'b1), .S(S0), .Count(fulladder_1_count));
  not not_2 (not_2_out, Y1);
  Fulladder fulladder_2 (.A(X1), .B(not_2_out), .Cin(fulladder_1_count), .S(S1), .Count(fulladder_2_count));
  Seven_Seg_Hex seven_seg_hex_2 (.d({S3, S2, S1, S0}), .dp(1'b0));
  not not_3 (not_3_out, Y2);
  Fulladder fulladder_3 (.A(X2), .B(not_3_out), .Cin(fulladder_2_count), .S(S2), .Count(fulladder_3_count));
  not not_4 (not_4_out, Y3);
  Fulladder fulladder_4 (.A(X3), .B(not_4_out), .Cin(fulladder_3_count), .S(S3), .Count(Count));
  Seven_Seg_Hex seven_seg_hex_3 (.d({Y3, Y2, Y1, Y0}), .dp(1'b0));
endmodule
